# Fritzing sketch calibration (saved by Fritzing 0.9.3b)

parts:
  Arduino = Arduino Uno (Rev3) - ICSP
  R1 = Resistor [tolerance=±5% resistance=500 package=THT]
  110v_Plug_(EC)1 = female pin header, 2 pins [form="♀ (female)"]
  R2 = Resistor [tolerance=±5% resistance=2.2k package=THT]
  WaterTemp = DS18B20 1-Wire Temperature Sensor Probe Cable

nets:
  N1: Arduino.A0, R1.Pin_1, 110v_Plug_(EC)1.pin1
  N2: Arduino.A1, R1.Pin_0
  5V: Arduino.5V, R2.Pin_0, WaterTemp.VDD
  GND: Arduino.GND, 110v_Plug_(EC)1.pin2, WaterTemp.GND
  N3: Arduino.D10_PWM/SS, R2.Pin_1, WaterTemp.DQ
