# Fritzing sketch hydroponics (saved by Fritzing 0.9.3b)
breadboards: 1

parts:
  ESP-01 = ESP8266 WiFi Module [part_number=ESP8266]
  C1_-_100uf = Capacitor Polarized [package=cpol-radial-100uf-25v]
  R2 = Resistor [tolerance=±5% resistance=3.3k package=THT]
  IC1 = V_REG_LD1117VXX [package=78xxl]
  PhotoCell = Photocell (LDR) [package=THT]
  IC2 = IC, DIP package, 4 pins [chip_label=AMT1001]
  R3 = Resistor [tolerance=±5% resistance=10k package=THT]
  Water_Pump_Relay = KY-019 5V Relay Module [package="Breakout board"]
  LLC = Logic Level Converter
  R4 = Resistor [tolerance=±5% resistance=500 package=THT]
  WaterTemp_&_EC = DS18B20 1-Wire Temperature Sensor Probe Cable
  110v_Plug_(EC) = female pin header, 2 pins [form="♀ (female)"]
  Nano = Arduino Nano (Rev3.0)
  YF-S201_Flow_Meter1 = YF-S201 Water Flow Meter
  Float_Sensor = Round Pushbutton
  R5 = Resistor [tolerance=±5% resistance=1k package=THT]
  R6 = Resistor [tolerance=±5% resistance=1k package=THT]
  Water_Pump_(220v) = DC Motor
  Wall = AC Power [voltage=220 frequency=60]
  Manual_WaterPump_Start = Round Pushbutton
  C2_-_1000uf = Capacitor Polarized [package=cpol-radial-100uf-25v]
  R7 = Resistor [tolerance=±5% resistance=2.2k package=THT]

nets:
  N1: ESP-01.RXD, LLC.RX_LV
  N2: ESP-01.VCC, ESP-01.RST, ESP-01.CH_PD, C1_-_100uf.+, IC1.OUT, LLC.LV
  GND: ESP-01.GND, C1_-_100uf.-, R2.Pin_0, IC1.GND, IC2.pin2, R3.Pin_0, Water_Pump_Relay.-, LLC.GND, WaterTemp_&_EC.GND, 110v_Plug_(EC).pin2, Nano.GND, YF-S201_Flow_Meter1.GND, R5.Pin_0, C2_-_1000uf.-
  N3: ESP-01.TXD, LLC.TX_LV
  N4: R2.Pin_1, PhotoCell.pin_0, Nano.A5
  5V: IC1.IN, PhotoCell.pin_1, IC2.pin1, Water_Pump_Relay.+, LLC.HV, WaterTemp_&_EC.VDD, Nano.VIN, YF-S201_Flow_Meter1.VCC, Float_Sensor.leg1, R6.Pin_1, C2_-_1000uf.+, R7.Pin_0
  N5: IC2.pin3, R3.Pin_1, Nano.A7
  N6: IC2.pin4, Nano.A6
  N7: Water_Pump_Relay.S, Nano.D4, R6.Pin_0
  N8: Water_Pump_Relay.NC, Manual_WaterPump_Start.leg0
  N9: Water_Pump_Relay.Common, Water_Pump_(220v).pin_1
  N10: Water_Pump_Relay.NO, Wall.V+, Manual_WaterPump_Start.leg1
  N11: LLC.TX_HV, Nano.D1/TX
  N12: LLC.RX_HV, Nano.D0/RX
  N13: R4.Pin_0, Nano.A1
  N14: R4.Pin_1, 110v_Plug_(EC).pin1, Nano.A0
  N15: WaterTemp_&_EC.DQ, Nano.D10, R7.Pin_1
  N16: Nano.D3, Float_Sensor.leg0, R5.Pin_1
  N17: Nano.D5, YF-S201_Flow_Meter1.SIG
  N18: Water_Pump_(220v).pin_2, Wall.V-

custom parts:
  ESP8266 WiFi Module: Generic WiFi Module based on the ESP8266 with onboard PCB antenna and UART communications
  KY-019 5V Relay Module: KY-019 5V Relay module, used to control AC circuits.
  YF-S201 Water Flow Meter: The YF-S201 Flow Meter. The input voltage is 5V to 24V (DC).
