# Fritzing sketch ftd-esp01 (saved by Fritzing 0.9.3b)
breadboards: 1

parts:
  ESP-01 = ESP8266 WiFi Module [part_number=ESP8266]
  FTD1232 = FTDI Basic Programmer
  Flash = SWITCH-MOMENTARY-2 [package=tactile_switch_smd-2]
  Reset = SWITCH-MOMENTARY-2 [package=tactile_switch_smd-2]
  V1 = DC Power [voltage=3.3V]
  R1 = Resistor [tolerance=±5% resistance=1k package="0603 [SMD]"]
  R2 = Resistor [tolerance=±5% resistance=1k package="0603 [SMD]"]
  C1_-_100uf = Capacitor Polarized [package=cpol-radial-100uf-25v]

nets:
  N1: ESP-01.RXD, FTD1232.TXO
  N2: ESP-01.VCC, ESP-01.CH_PD, FTD1232.POWER, V1.V+, R1.Pin_1, R2.Pin_1, C1_-_100uf.+
  N3: ESP-01.GPIO_0, Flash.2, R1.Pin_0
  N4: ESP-01.RST, Reset.2, R2.Pin_0
  GND: ESP-01.GND, FTD1232.GND, Reset.1, V1.V-
  N5: ESP-01.TXD, FTD1232.RXI
  GND_2: Flash.1, C1_-_100uf.-

custom parts:
  ESP8266 WiFi Module: Generic WiFi Module based on the ESP8266 with onboard PCB antenna and UART communications
