# Fritzing sketch hydroponics (saved by Fritzing 0.9.3b)
perfboards: 1

parts:
  ESP-01 = ESP8266 WiFi Module [part_number=ESP8266]
  C1_-_100uf = Capacitor Polarized [package=cpol-radial-100uf-25v]
  R2 = Resistor [tolerance=±5% resistance=680 package=THT]
  IC1 = V_REG_LD1117VXX [package=78xxl]
  PhotoCell = Photocell (LDR) [package=THT]
  IC2 = IC, DIP package, 4 pins [chip_label=AMT1001]
  R3 = Resistor [tolerance=±5% resistance=10k package=THT]
  Water_Pump_Relay = KY-019 5V Relay Module [package="Breakout board"]
  R4 = Resistor [tolerance=±5% resistance=500 package=THT]
  WaterTemp_&_EC = DS18B20 1-Wire Temperature Sensor Probe Cable
  110v_Plug_(EC) = female pin header, 2 pins [form="♀ (female)"]
  Nano = Arduino Nano (Rev3.0)
  YF-S201_Flow_Meter1 = YF-S201 Water Flow Meter
  Float_Sensor = Round Pushbutton
  R5 = Resistor [tolerance=±5% resistance=1k package=THT]
  R6 = Resistor [tolerance=±5% resistance=1k package=THT]
  Water_Pump_(220v) = DC Motor
  Wall = AC Power [voltage=220 frequency=60]
  Manual_WaterPump_Start = Round Pushbutton
  C2_-_1000uf = Capacitor Polarized [package=cpol-radial-100uf-25v]
  R7 = Resistor [tolerance=±5% resistance=2.2k package=THT]
  Part1 = Logic Level Converter
  FAULT = LED - 3mm [color="Red (633nm)" package="3 mm [THT]"]
  R8 = Resistor [tolerance=±5% resistance=330 package=THT]
  STATUS = LED - 3mm [color="Blue (470nm)" package="3 mm [THT]"]
  R9 = Resistor [tolerance=±5% resistance=330 package=THT]
  ZS-042_RTC1 = ZS-042 RTC Module

nets:
  N1: ESP-01.RXD, Part1.TX_LV
  3.3V: ESP-01.VCC, ESP-01.RST, ESP-01.CH_PD, C1_-_100uf.+, IC1.OUT, Part1.LV
  GND: ESP-01.GND, C1_-_100uf.-, R2.Pin_0, IC1.GND, IC2.pin2, R3.Pin_0, Water_Pump_Relay.-, WaterTemp_&_EC.GND, 110v_Plug_(EC).pin2, Nano.GND, YF-S201_Flow_Meter1.GND, R5.Pin_0, R6.Pin_1, C2_-_1000uf.-, Part1.GND, FAULT.cathode, STATUS.cathode, ZS-042_RTC1.GND
  N2: ESP-01.TXD, Part1.RX_LV
  N3: R2.Pin_1, PhotoCell.pin_0, Nano.A3
  5V: IC1.IN, PhotoCell.pin_1, IC2.pin1, Water_Pump_Relay.+, WaterTemp_&_EC.VDD, Nano.VIN, YF-S201_Flow_Meter1.VCC, Float_Sensor.leg1, C2_-_1000uf.+, R7.Pin_0, Part1.HV
  N4: IC2.pin3, R3.Pin_1, Nano.A7
  N5: IC2.pin4, Nano.A6
  N6: Water_Pump_Relay.S, Nano.D4, R6.Pin_0
  N7: Water_Pump_Relay.NC, Manual_WaterPump_Start.leg0
  N8: Water_Pump_Relay.Common, Water_Pump_(220v).pin_1
  N9: Water_Pump_Relay.NO, Wall.V+, Manual_WaterPump_Start.leg1
  N10: R4.Pin_0, Nano.A1
  N11: R4.Pin_1, 110v_Plug_(EC).pin1, Nano.A0
  N12: WaterTemp_&_EC.DQ, Nano.D10, R7.Pin_1
  N13: Nano.D1/TX, Part1.RX_HV
  N14: Nano.D0/RX, Part1.TX_HV
  N15: Nano.RESET, Nano.D8
  N16: Nano.D2, YF-S201_Flow_Meter1.SIG
  N17: Nano.D3, Float_Sensor.leg0, R5.Pin_1
  N18: Nano.D5, R9.Pin_1
  N19: Nano.D6, R8.Pin_1
  N20: Nano.D7, ZS-042_RTC1.VCC
  N21: Nano.A5, ZS-042_RTC1.SCL
  N22: Nano.A4, ZS-042_RTC1.SDA
  N23: Water_Pump_(220v).pin_2, Wall.V-
  N24: FAULT.anode, R8.Pin_0
  N25: STATUS.anode, R9.Pin_0

custom parts:
  ESP8266 WiFi Module: Generic WiFi Module based on the ESP8266 with onboard PCB antenna and UART communications
  KY-019 5V Relay Module: KY-019 5V Relay module, used to control AC circuits.
  YF-S201 Water Flow Meter: The YF-S201 Flow Meter. The input voltage is 5V to 24V (DC).
